# Fritzing sketch Wiring (saved by Fritzing 0.9.3b)

parts:
  Part1 = Adafruit Gemma M0 [part_number="Adafruit #3501"]
  Part2 = 16 NeoPixel Ring [part_number=1463]

nets:
  3.3V: Part1.3.3V, Part2.VDD
  N1: Part1.D1_A0, Part2.IN
  GND: Part1.GND, Part2.GND

custom parts:
  Adafruit Gemma M0: The Adafruit Gemma M0 is a super small microcontroller board, with just enough built-in to create many simple projects. It may look small and cute: round, about the size of a quarter, with friendly alligator-clip sew pads. But do not be fooled! The Gemma M0 is incredibly powerful! We've taken the same form factor we used for the original ATtiny85-based Gemma and gave it an upgrade. The Gemma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
  16 NeoPixel Ring: 16 ultra bright smart LED NeoPixels are arranged in a circle with 1.75" (44.5mm) outer diameter. The rings are 'chainable' - connect the output pin of one to the input pin of another. Use only one microcontroller pin to control as many as you can chain together! Each LED is addressable as the driver chip is inside the LED. Each one has ~18mA constant current drive so the color will be very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
